# Fritzing sketch product sketch (saved by Fritzing 0.9.3b)
circuit board: 7.07613cm x 5.53644cm
perfboards: 2

parts:
  Arduino_PCB = Arduino Uno (Rev3) - ICSP
  Bauteil2 = DB25F
  moisture_sensor = Infrared Proximity Sensor
  resistor_220_Ohm = Resistor [tolerance=±5% resistance=220 package=THT]
  red_soil_is_dry = LED - 5mm [color="Red (633nm)" package="5 mm [THT]"]
  green_currently_measurement = LED - 5mm [color="Green (555nm)" package="5 mm [THT]"]
  Bauteil3 = DB25M
  M1 = DC Motor
  J3 = male pin header, 1 pin [form="♂ (male)"]
  J2 = male pin header, 1 pin [form="♂ (male)"]
  J1 = male pin header, 3 pins [form="♂ (male)"]
  J4 = male pin header, 1 pin [form="♂ (male)"]
  Q1 = PNP-Transistor [package="TO92 [THT]"]
  J6 = male pin header, 1 pin [form="♂ (male)"]
  J7 = male pin header, 1 pin [form="♂ (male)"]
  J9 = male pin header, 1 pin [form="♂ (male)"]
  J8 = male pin header, 1 pin [form="♂ (male)"]
  J10 = male pin header, 1 pin [form="♂ (male)"]
  J11 = female pin header, 4 pins [form="♀ (female)"]
  J12 = female pin header, 3 pins [form="♀ (female)"]
  J13 = female pin header, 3 pins [form="♀ (female)"]
  J14 = female pin header, 2 pins [form="♀ (female)"]
  J15 = female pin header, 3 pins [form="♀ (female)"]

nets (from the breadboard view):
  N1: Arduino_PCB.A4/SDA, Bauteil2.pin3, moisture_sensor.GND, Bauteil3.pin3, J4.pin1, J14.pin1
  N2: Arduino_PCB.ICSP_SCK, Arduino_PCB.D13/SCK, Bauteil2.pin9, green_currently_measurement.anode, Bauteil3.pin9, J8.pin1, J13.pin1
  N3: Arduino_PCB.ICSP_MOSI, Arduino_PCB.D11_PWM/MOSI, Q1.B, J10.pin1, J13.pin3
  N4: Arduino_PCB.GND, Bauteil2.pin2, Bauteil2.pin5, Bauteil2.pin10, moisture_sensor.Vout, green_currently_measurement.cathode, Bauteil3.pin2, Bauteil3.pin5, Bauteil3.pin10, M1.pin_2, J3.pin1, J1.pin1, J1.pin2, J1.pin3, J7.pin1, J15.pin3
  N5: Arduino_PCB.D0/RX, J11.pin4
  N6: Arduino_PCB.D1/TX, J11.pin3
  N7: Arduino_PCB.D2, J11.pin2
  N8: Arduino_PCB.D3_PWM, J11.pin1
  N9: Arduino_PCB.D5_PWM, Bauteil2.pin1, moisture_sensor.Vcc, Bauteil3.pin1, J2.pin1, J12.pin3
  N10: Arduino_PCB.D7, resistor_220_Ohm.Pin_0, J12.pin1
  N11: Arduino_PCB.5V, Q1.C, J15.pin1
  N12: Bauteil2.pin4, Bauteil3.pin4, M1.pin_1, Q1.E, J6.pin1
  N13: Bauteil2.pin11, resistor_220_Ohm.Pin_1, red_soil_is_dry.anode, Bauteil3.pin11, J9.pin1
  N14: Bauteil2.pin12, red_soil_is_dry.cathode, Bauteil3.pin12

notes:
  vegetronix VH400 soil moisture sensor with
  voltage input (red)
  data output (black)
  ground (naked wire)
  http://vegetronix.com/Products/VH400/
  indicator that the soil is dry
  Power Pin D7
  vegetronix VH400 PCB wireing
  D0 = voltage input
  ground = ground
  A5 = data output / data input
  Read the moisture analog input value from the moisture sensor on A4
  indicator that currently a moisture measurement is performed
  Power Pin D13
  nanismus
  green : currently measurement
  red : soil is dry
  resistor : 220 Ohm
  moisture sensor
  Low Voltage under water pump from Barwig
  600 l/h
  voltage input
  ground
  https://www.conrad.de/de/niedervolt-tauchpumpe-barwig-0444-600-lh-6-m-539090.html
  give power to the moisture sensor
  Power Pin D5
  Indication LED
  Shows that a moisture measurement is currently performed
  PIN D13
  Indication LED
  Shows that the soil is dry
  Pin D7
  give power to the transistor to switch the 5 V power supply for the water pump
  Power Pin D11
  Transistor to switch the 5 V input for the water pump
  The digital Power I/O Pins don't provide enough current to start the pump
  Transistor BC635 / FBB07
  RedFly Shield from watterott
  https://github.com/watterott/RedFly-Shield

// code stored in the sketch: nanismusPCB.ino
//
// nanismusPCBcode
//
// Code to run on the Arduino PCB
// Developed with [embedXcode](http://embedXcode.weebly.com)
//
// Author 		Stefan Willuda
// 				Stefan Willuda
//
// Date			01.08.16 14:31
// Version		0.66.0
//
// Copyright	© Stefan Willuda, 2016
// Licence		Creative Commons - Attribution - ShareAlike 3.0
//
// See          ReadMe.txt


/* current result of arduino IDE compiling
 Der Sketch verwendet 13.948 Bytes (43%) des Programmspeicherplatzes. Das Maximum sind 32.256 Bytes.
 Globale Variablen verwenden 673 Bytes (32%) des dynamischen Speichers, 1.375 Bytes für lokale Variablen verbleiben. Das Maximum sind 2.048 Bytes.
 */


// PIN Declaration ################################################################################################################


// Declaration of the Pins for the RedFly WiFi Shield


// D0, D1, D2, D3 // https://github.com/watterott/Arduino-Libs/tree/master/RedFly




// Declarations for status indicators LEDs


// D5
#define SoilMeasureVoltagePin 5 // Pin to start the moisture measurement


// D7
#define SoilDryWarningLED 7 // LED that indicated dryness in the soil


// D11
#define PumpVoltagePin 11 // Pin to start the waterpump to water the soil


// D13
#define CurrentlyMoistureMeasurementIndicatorLED 13 // LED that indicates that right now a moisture measurement is performed


// A4
#define MoistureMeasurementAnalogInputPin 4




// Include Libraries ###############################################################################################################




// Include Arduino library to allow autocomplete syntax in Xcode
#include <Arduino.h>


// Include libraries to allow WiFi Connection with the RedFly Wifi shield
// https://github.com/watterott/Arduino-Libs/tree/master/RedFly
#include <RedFly.h>
#include <RedFlyClient.h>
#include <RedFlyServer.h>




// Constants and variables ##########################################################################################################




// define if this is a test build or a production build
#define test 0 // 0 == production ; 1 == test
/* the interpretation of this value will currently lead to a different http POST statement
 * which writes differently attributed data to the database
 */


// Calculate or store constants that are uses several times in the codebase


// When we apply voltage to the moisture sensor it takes a short time for the sensor to adjust
unsigned long SoilMoistureMeasurementWaitDuration = 1000; // milliseconds 1.000 milliseconds = 1 second




// Every how many milliseconds are we going to perform a moisture measurement?
// currently I use millis() because I don't need the exact time and millis() is easier to simulate than now()
// 30 minutes * 60 seconds * 1000 milliseconds
unsigned long MoistMeasureInterval = 1800000; // 30 * 60 * 1000; // milliseconds 1.000 milliseconds = 1 second


// store the most recent time when the moisture measurement took place
/* When we start the first iteration of the code loop than we use the current time minus one interval
 * which leads to an immediate measurement of the soil when the board is connected to the power supply
 */
long lastMoistMeasureTime = -1 * MoistMeasureInterval;




// define the variable that stores the data input that is sent by the soil moisture sensor for reuseage
int MoistureMeasurementResultAnalogInput;




// Define the thresholds of different analog input values to decide if they can be considered as dry, moist and so on...
/* This array shall be extended later if we want a more granular distinction between dry, moist, toomoist soil
 * How to calculate the actual voltage input is well described at https://www.arduino.cc/en/Tutorial/ReadAnalogVoltage
 */
/* to define the thresholds for the analogInput value of the moisture sensor
 * I've measured the voltage input in a glass of water, which I consider to be wet and it was 0.7 volts input
 * Considering the formular: voltage= sensorValue * (5.0 / 1023.0)
 * I've measured different states of moisture to collect example data
 * If the moisture sensor sticks to really dry soil = 10% wet = 1,0 V
 *      0% moist = 1,00 V = 205 analogInput
 * If the moisture sensor sticks in soil that is considered 40% wet = 1,66 V
 *		40% moist = 1,66 V = 340 analogInput
 * If the moisture sensor sticks in soil that has been watered right now = 2,16 V
 *		80% moist = 2,16 V = 442 analogInput
 * If the moisture sensor sticks in soil that is still water wet after a watering = 2,35 V
 *		100% moist = 2,35 V = 481 analogInput
 * If the moisture sensor sticks in a glass of water I can measure with a multimeter 2.6 Volts input
 *		water moist = 2.6 V = 532 analogInput


 * This definition was adjusted on the 15th August to
 
 * Used thresholds
 
 * "zero water" : 0% : 240 : Indicator 0 - urgently dry
 * "urgently dry" : 20% : 300 : Indicator 0 - urgently dry
 * "moist" : 40% : 380 : Indicator 1 - dry
 * "very moist" : 80% : 442 : Indicator 2 - moist
 * "wet" : 100% : 481 : Indicator 2 - moist
 */
int ThresholdsForAnalogInputValues[] = {240, 300, 380, 442, 481};


/* In the Array we store different tresholds
 * position 0 --> the indicator for "urgently dry" - triggers self watering event
 * position 1 --> the indicator for "dry" - triggers the red warning lamp that asks for manual watering
 * position 2 --> the indicator for "moist" - everything is ok
 */
int MoistureIndicators[] = {0, 1, 2};


/* Store the indicator of the soil moisture
 * When we run the loop for the first time we consider the soil to be "moist";
 */
int MoistureIndicator = MoistureIndicators[2];




// Debug Functions ####################################################################################################################




//debug output functions (9600 Baud, 8N2)
//Leonardo boards use USB for communication, so we dont need to disable the RedFly
void debugout(char *s)
{


    RedFly.disable();
    Serial.print(s);
    RedFly.enable();
    
}


/* By using the RedFly WiFi Shield we have communications conflicts with 
 * serial communication. That is why we have do shortly disable the RedFly Shield when 
 * doing a serial print
 */
void debugoutln(char *s)
{
#if defined(__AVR_ATmega32U4__)
    Serial.println(s);
#else
    RedFly.disable();
    Serial.println(s);
    RedFly.enable();
#endif
}




// Establish a WiFi Connection using the RedFly WiFi Shield ##########################################################################




void EstablishWifiConnectionWithRedFlyShield()
{
    
    // initialize the WiFi module on the shield
    
    // Serial log
    // debugoutln("EstablishWiFiConnectionWithRedFlyShield()");
    
    uint8_t ret;
    
    //init the WiFi module on the shield
    // ret = RedFly.init(br, pwr) //br=9600|19200|38400|57600|115200|200000|230400, pwr=LOW_POWER|MED_POWER|HIGH_POWER
    // ret = RedFly.init(pwr) //9600 baud, pwr=LOW_POWER|MED_POWER|HIGH_POWER
    // ret = RedFly.init() //9600 baud, HIGH_POWER
    
    ret = RedFly.init();
    
    /* sometimes the connection is not established on the first try, thats why I need to try more than once
     * but not more than maxcounter times, because this would make the whole code in the loop stop
     */
    
    int counter, maxcounter;
    counter = 0;
    maxcounter = 50;
    
    while (ret && counter < maxcounter) {
        
        ret = RedFly.init();


        debugoutln("RedFly.init ERROR"); //there are problems with the communication between the Arduino and the RedFly


        counter++;
        
    }
    
    if(ret){


        // debugoutln("RedFly.init ERROR"); //there are problems with the communication between the Arduino and the RedFly
        
    }
    else {
        
        // scan for wireless networks (must be run before join command)
        RedFly.scan();
        
        
        //join network
        // ret = join("wlan-ssid", "wlan-passw", INFRASTRUCTURE or IBSS_JOINER or IBSS_CREATOR, chn, authmode) //join infrastructure or ad-hoc network, or create ad-hoc network
        // ret = join("wlan-ssid", "wlan-passw", IBSS_CREATOR, chn) //create ad-hoc network with password, channel 1-14
        // ret = join("wlan-ssid", IBSS_CREATOR, chn) //create ad-hoc network, channel 1-14
        // ret = join("wlan-ssid", "wlan-passw", INFRASTRUCTURE or IBSS_JOINER) //join infrastructure or ad-hoc network with password
        // ret = join("wlan-ssid", INFRASTRUCTURE or IBSS_JOINER) //join infrastructure or ad-hoc network
        // ret = join("wlan-ssid", "wlan-passw") //join infrastructure network with password
        // ret = join("wlan-ssid") //join infrastructure network
        
        
        #define Network "WLAN-Kabel"
        #define NetworkPW "1604644462468036"
 
        ret = RedFly.join(Network, NetworkPW, INFRASTRUCTURE);
        
        /* sometimes the connection is not established on the first try, thats why I need to try more than once
         * but not more than maxcounter times, because this would make the whole code in the loop stop
         */
        
        // reset the counter
        counter = 0;
        
        while (ret && counter < maxcounter) {
            
            ret = RedFly.join(Network, NetworkPW, INFRASTRUCTURE);
            
            debugoutln("RedFly.join ERROR");
            
            counter++;
            
        }
        
        if(ret){
            
            //debugoutln("RedFly.join ERROR");
            
        }
        else {
           
            /*
            byte ip[]        = { 192, 168, 178, 34 }; //ip from shield (client)
            byte netmask[]   = { 255, 255, 255,  0 }; //netmask
            byte gateway[]   = { 192, 168, 178,  1 }; //ip from gateway/router
            byte dnsserver[] = { 192, 168, 178,  1 }; //ip from dns server
            byte server[]    = {   0,  0,  0,  0 }; //{  85, 13,145,242 }; //ip from www.watterott.net (server)
            
             */
            
            //set ip config
            // ret = RedFly.begin(); //DHCP
            // ret = RedFly.begin(1 or 2); //1=DHCP or 2=Auto-IP
            // ret = RedFly.begin(ip);
            // ret = RedFly.begin(ip, dnsserver);
            // ret = RedFly.begin(ip, dnsserver, gateway);
            // ret = RedFly.begin(ip, dnsserver, gateway, netmask);
            
            ret = RedFly.begin();


            /* sometimes the connection is not established on the first try, thats why I need to try more than once
             * but not more than 20 times, because this would make the whole code in the loop stop
             */
            
            counter = 0;
            
            while (ret && counter < maxcounter) {
                
                ret = RedFly.begin();
                
                debugoutln("RedFly.begin ERROR");
                
                counter++;
                
            }
            
            if(ret){
                
                // The connection was not established this time, so disconnect
                // RedFly.disconnect();
                
            }
            else {
                
                //RedFly.getlocalip(ip);       // receive shield IP in case of DHCP/Auto-IP
                
                // server.begin();
                debugoutln("WiFi Shield connected");
                
            }
        }
    }
}




// Send out the measured data to a website ###########################################################################################




/* Sends different values to a http webserver on which a PHP script waits for the data
 * to store them in a MySQL database
 
 * Based on Watterott sample
 * Web Client
 * This sketch connects to a website using a RedFly-Shield.
 
 * Inspired by
 * http://jleopold.de/wp-content/uploads/2011/03/ArduinoDatenLogger.txt
 */




// Check if we receive a HTTP response for our POST request and interprete this response
// return true if the data transmission was successful, else return false
boolean SuccessOfHttpPostRequest(RedFlyClient client){
    
    // interprete the result of the http response to store the return value of this function
    boolean tempReturnValue;
    
    
    /* To be sure that the data transmission was successful catch the server response and evaluate the result
     * oriented on the RedFly Example WebClient.ino
     * I did not want to use the loop() to evaluate the server response
     * That is why I chose to use a while() with a timeout
     * If there is no response within the timeout, I have to asume that the server is not available
     */
    
    // Timekeeper to check if the Timeout is reached
    unsigned long currentMillis = millis();
    unsigned long startTime = currentMillis;
    
    // give it a TimeoutTime milliseconds to receive an answer from the webserver
    unsigned long TimeoutTime = 120000; // milliseconds
    
    /* The Webserver is going to answer with a simple HTTP response
     * We are going to fetch the answer in a buffer
     * and then we are going to check the server HTTP response if we get a "success" response or something else
     */
    
    // declarations to process the answer of the webserver
    char data[300];  //receive buffer, usually the answer is not larger than 250 chars
    unsigned int len=0; //receive buffer length
    
    /* We are going to seach in the HTTP response for a phase that indicates transmission success
     * Therefore we are looking for a pointer, which indicates the position in the array that holds
     * the match
     */
    // Size of the Pointer, is greater that 0 in every case we receive data from the webserver
    int PointerSize = 0;
    
    // indicator that the webserver is transmitting a response
    int c;
    
    // Serial log info
    debugoutln("start waiting");
    
    
    /* Start the while()
     * As long as we don't get an response or the TimeoutTime is not exeeded, we keep waiting for a response
     * PointerSize is larger than 0 whenever we receive a HTTP response
     * Even if we receive a HTTP response that does not indicate transmission success, we stop the while()
     * because we only want to interprete the answer. It is not necessary to waste time
     */
    while ((currentMillis - startTime <= TimeoutTime) && (PointerSize == 0)) {
        
        
        /*if there are incoming bytes available
         * from the server then read them
         */
        if(client.available()) {
            do
            {
                c = client.read();
                if((c != -1) && (len < (sizeof(data)-1)))
                {
                    // collect the whole HTTP response in the data array
                    data[len++] = c;
                }
            }while(c != -1);
        }
        
        //if the server's disconnected, stop the client and evaluate the received data
        if(len && !client.connected()) {
            
            client.stop();
            RedFly.disconnect();
            
            data[len] = 0;
            // Serial log info
            // debugout(data);
            
            
            /* Now that we received the HTTP response it is time to interprete the received data
             * The webserver we address is responding wether a "success", a "failure" or something else
             * We need to search in the HTTP response for that "success" or "failure" statement
             * It is not enough to receive a "200 OK" response, because this does only indicate, if we
             * have been able to connect to the webserver. Even if we receive a "failure" response
             * this will come with a "200 OK" response. That's why we have to dive a little bit deeper
             * and analyse the resonse message
             *
             * The idea is to find a specific substrting in a string with char datatype
             * this is described here http://forum.arduino.cc/index.php?topic=394718.0
             *
             * With that in mind we can search for any sub char array within the HTTP response array.
             */
            
            /* Answer, we need to receive in order to know that the submission was successful
             * This string is determinded in the "valueget.php" file on the webserver.
             */
            char successStringWebserver[] = "transmission success";
            
            // Pointer that locates the position of the searched substring (char array) within a larger char array
            char * Pointer;
            
            // function to find the pointer - is empty if there is no match
            Pointer = strstr(data, successStringWebserver);
            
            // To get out of the while() I have to check if we received a valid response from the webserver
            PointerSize = sizeof(Pointer);
            
            // We locate the position of the substring within the larger
            int PointerPosition;
            // subtract the starting pointer of Haystack from the pointer returned by strstr()
            PointerPosition = (&Pointer[0] - &data[0]);
            
            // The PointerPosition in the array is always positive if we find the substring in the larger dara array
            if (PointerPosition >= 0) {
                
                // transmission success
                // Serial Log info
                // debugoutln(successStringWebserver);
                
                // store the result to use it when the function is done
                tempReturnValue = true;
                
            }
            else if (PointerPosition < 0) {
                
                // Serial Log info
                // debugoutln("transmission failed");
                
                /* This means that we have been able to connect to the web server and POST our request
                 * but the response was not a success message.
                 * The reason for that might be, that the key to perform the database insert was wrong
                 * or that the script in valueget.php does not support the request URL
                 */
                
                // store the result to use it when the function is done
                tempReturnValue = false;
                
            }
            else {
                
                // Serial log info
                // debugoutln("something is wrong here");
                
                /* Actually this else event should not occur, because we only get here if we receive a
                 * response. But I don't want to let special events to be unhandled.
                 */
                
                // store the result to use it when the function is done
                tempReturnValue = false;
                
            }
            
            len = 0;
        }
        
        currentMillis = millis();
    }
    
    // serial log info
    debugoutln("stopped waiting");
    
    // flush the client connection
    // https://www.arduino.cc/en/Reference/WiFiClientFlush
    client.flush();
    
    return (tempReturnValue);
}




/* This function puts together all the different parts of the POST request
 * that is sent to the webserver
 */
char * assembleThePostRequest(int value) {
    
    
    // Host IP of web server. We use the static IP and avoid DNS resolution because we know the static IP of the server
#define HOSTNAME "192.168.178.24"
 
    // one is the name of the sensor (plant)
    const char * sensor_string;
    
    // we fill in different datatable values based on wether we have a test build or a production build
    if (test == 1){
        sensor_string = "Test";
    }
    else if (test == 0){
        sensor_string = "Banane";
    }
    
    // one is the kind of value we are transmitting
    const char * type_string;
    type_string = "Prozentfeuchte";
    
    
    //String GetRequest;
    // http://miscsolutions.wordpress.com/2011/10/16/five-things-i-never-use-in-arduino-projects/
    
    char * GetRequest;
    const char * get1;
    
    // Define the different values of the POST request
    
    //get1 = "GET /valueget.php";
    // Change from GET to POST, I've read something about security issues with GET
    get1 = "POST /valueget.php";
    
    const char * get2 = "?name=";
    const char * get3 = "&type=";
    const char * get4 = "&value=";
    const char * get5 = "&key=c3781633f1fb1ddca77c9038d4994345";//c3781633f1fb1ddca77c9038d4994345
    const char * get6 = " HTTP/1.1\r\nHost: ";
    const char * get7 = "\r\n\r\n";
    
    // transform the sensor value into a char to fit it in the POST request
    char * value_char;
    value_char = (char*) calloc(5, sizeof(char));
    itoa(value, value_char, 10);
    
    // allocate memory for the POST request
    GetRequest = (char*) calloc(strlen(get1) + strlen(get2) + strlen(sensor_string)  + strlen(get3) + strlen(type_string) + strlen(get4)
                                + strlen(value_char) + strlen(get5) + strlen(get6) + strlen(HOSTNAME) + strlen(get7) + 1, sizeof(char));
    
    // assemble the POST Request
    strcat(GetRequest, get1);
    strcat(GetRequest, get2);
    strcat(GetRequest, sensor_string);
    strcat(GetRequest, get3);
    strcat(GetRequest, type_string);
    strcat(GetRequest, get4);
    strcat(GetRequest, value_char);
    strcat(GetRequest, get5);
    strcat(GetRequest, get6);
    strcat(GetRequest, HOSTNAME);
    strcat(GetRequest, get7);
    
    return (GetRequest);
    
    // free the allocated string memory
    // free(GetRequest);
    // free(value_char);
    
}


// Here we do the  Http POST request and check if the transmission was successful
boolean HttpPostRequest(int value, RedFlyClient client, byte server[]){
    
    // debugoutln("HttpPostRequest");
    
    char * PostRequest = assembleThePostRequest(value);
    
    // we want to know if the transmission was successful
    boolean tempReturnValue;
    
    // connect the client to the web server and transmit the post request
    if(client.connect(server, 80))
    {
        //make a HTTP request
        //http://www.watterott.net/forum/topic/282
        
        // Serial log info
        // debugoutln("Http Send");
        
        // call the web server
        // Example request http://nanismus.no-ip.org/nanismus_test/valueget.php?name=Banane&type=status&value=6&key=123
        client.print(PostRequest);
        
        tempReturnValue = SuccessOfHttpPostRequest(client);
        
    }
    else {
        
        // Serial Log info
        debugoutln("server unavailable");
        
        // try to re-establish the wifi connection
        EstablishWifiConnectionWithRedFlyShield();
        
        tempReturnValue = false;
        
    }
    
    // free allocated memory
    free(PostRequest);
    
    return (tempReturnValue);
    
}


// define the address of the server and trigger a POST request to a webserver
/* we try to send the value to the webserver
 * if this does not work out on the first try we try it again with the same value
 * if this again does not work out, we try to re-establish the whole Wifi connection
 * unfortunately we currently cannot do more than that because we don't have access to
 * the server */
void FullHttpPostTransmission(int value){
    
    /* Server IP adress - we remain with a local IP because currently the web server is
     * in the same network as the RedFly WiFi shield
     */
    byte server[] = { 192, 168, 178, 24 }; //{  85, 13,145,242 }; //ip from www.watterott.net (server)
    
    // initialize the client
    RedFlyClient client(server, 80);
    
    int maxAttempts = 4; // how often do we try to send out the data at max?
    int numberAttempts = 1; // starting point to count
    
    // if we could not transmit successfully try it again
    do {
        
        // Serial log info
        // debugoutln("new attempt to do a POST");
        
        // The Post request is done in the while statement below
        
        // count the number of attempts up
        numberAttempts++;
        
    }
    // Check if we receive a HTTP response for our POST request and interprete this response
    while (!HttpPostRequest(value, client, server) && (numberAttempts <= maxAttempts));
    
}




// Setup Start #######################################################################################################################




void setup() {
    
    // Inialize the Serial Communication and set the data rate for the hardware serial port
    Serial.begin(9600);
    
    // Statuslog
    // debugoutln("void setup()");
    
    // Define pins and functions of these pins
    pinMode(SoilDryWarningLED, OUTPUT);  // to switch on or off the LED for dryness indication
    pinMode(SoilMeasureVoltagePin, OUTPUT); // to apply voltage to the moisture sensor
    pinMode(CurrentlyMoistureMeasurementIndicatorLED, OUTPUT); // to switch on or off the LED for measurement indication
    pinMode(PumpVoltagePin, OUTPUT);
    
    // Blink once to show that we have the new version of the code
    digitalWrite(SoilDryWarningLED, HIGH);
    delay(400);
    digitalWrite(SoilDryWarningLED, LOW);
    
    // initially connect to the WiFi network using the RedFly WiFi Shield
    EstablishWifiConnectionWithRedFlyShield();
    
}




// Setup End #########################################################################################################################




/* Check if it is time to perform a new moisture measurement
 * We don't want to measure the moisture every loop of the processor
 */
boolean IsTimeForMoistureMeasurement() {
    
    // TRUE = Yes, we need to perform a moisture measurement
    // FALSE = No, currently no new moisture measurement needed, the last moisture measurement was performed not long ago
    
    /* If the time that has passed between the last moisture measurement and now is larger than
     * the defined moisture intervall than a new moisture measurement is needed
     */
    
    unsigned long currentMillis = millis();
    if(currentMillis - lastMoistMeasureTime >= MoistMeasureInterval) {
        return(true);
    }
    else {
        return(false);
    }
}


/* Interprete the return percentage value into an LED light indication if the soil is dry
 *
 */
// Interprete the analog input from the moisture sensor
void InterpreteMoistureMeasurementAnalogInput(int Input) {
    
    // Define wether a analog input value is considered dry or moist
    
    // Check if the analog input value from the moisture sensor is considered to indicate an "urgently dry" soil
    if(Input <= ThresholdsForAnalogInputValues[MoistureIndicators[1]]){
        
        // retun that the soil is considered "urently dry"
        MoistureIndicator = MoistureIndicators[0];
        
    }
    // Check if the analog input value from the moisture sensor is considered to indicate a "dry" soil
    else if(Input <= ThresholdsForAnalogInputValues[MoistureIndicators[2]]){
        
        // retun that the soil is considered "dry"
        MoistureIndicator = MoistureIndicators[1];
        
    }
    else {
        
        // return that the soil is considred "moist"
        MoistureIndicator = MoistureIndicators[2];
    }
}


/* Calculate the percentage value of current moisture based on the last measured moisture analog Input
 * This percentage value of the current moisture will be shown to the user on a website or in an app and so on... 
 */
long PercentMoistureValue(int AnalogInputValue)
{
    
    // see the threshold definition above
    int zero = ThresholdsForAnalogInputValues[0];
    int twenty = ThresholdsForAnalogInputValues[1];
    int fourty = ThresholdsForAnalogInputValues[2];
    int eighty = ThresholdsForAnalogInputValues[3];
    int hundred = ThresholdsForAnalogInputValues[4];
    
    long PercentageValue;
    
    /* If we ever receive an anlogInput value that is larger than 100% == 481 or smaller than 
     * 0% == 205 than we limit the range of the value we calculate with with the 0% and 100% values
     * which have been defined in the thresholds for the analog input values
     */
    AnalogInputValue = constrain(AnalogInputValue, zero, hundred);
    
    // percentage mapping between 0 and 20%
    // https://www.arduino.cc/en/Reference/Map
    if (AnalogInputValue <= twenty){
        PercentageValue = map(AnalogInputValue, zero, twenty, 0, 20);
    }
    // percentage mapping between 20 and 40%
    else if ((AnalogInputValue > twenty) && (AnalogInputValue <= fourty)){
        PercentageValue = map(AnalogInputValue, twenty + 1, fourty, 21, 40);
    }
    // percentage mapping between 40 and 80%
    else if ((AnalogInputValue > fourty) && (AnalogInputValue <= eighty)){
        PercentageValue = map(AnalogInputValue, fourty + 1 , eighty, 41, 80);
    }
    // percentage mapping between 80 and 100%
    else if (AnalogInputValue > eighty){
        PercentageValue = map(AnalogInputValue, eighty + 1, hundred, 81, 100);
    }
    
    return(PercentageValue);
}




// Start the actual moisture measurement by calling data from the moisture sensor
void PerformMoistureMeasurement(){
    
    // idicate with an LED that a measurement is currently performed
    digitalWrite(CurrentlyMoistureMeasurementIndicatorLED, HIGH);
    
    // apply voltage to soil moisture sensor
    digitalWrite(SoilMeasureVoltagePin, HIGH);
    
    /* wait for a short time that the soil moisture sensor can adjust
     * I know, that I could have used delay() but for some reasons I encounterd
     * timing problems with delays longer than 900 ms
     */
    // Therefore store the current time
    unsigned long currentMillis = millis();
    
    // store the beginning of this measurement
    unsigned long firstMeasureTime = currentMillis;
    
    // Go through a loop until the duration it takes to perform a moisture measurement is over
    while (currentMillis - firstMeasureTime < SoilMoistureMeasurementWaitDuration) {
        
        currentMillis = millis();
    }
    
    // collect the data input that is sent by the soil moisture sensor and store it for reuseage
    MoistureMeasurementResultAnalogInput = analogRead(MoistureMeasurementAnalogInputPin);
    
    // switch of the voltage of the moisture sensor
    digitalWrite(SoilMeasureVoltagePin, LOW);
    
    // switch off the indication LED
    digitalWrite(CurrentlyMoistureMeasurementIndicatorLED, LOW);
    
    // Interprete the analog input value from the sensor
    InterpreteMoistureMeasurementAnalogInput(MoistureMeasurementResultAnalogInput);
    
}




/* Measure the moisture of the soil
 * but only if it is already time to do the measurement
 */
void MoistureMeasurement(boolean IsTimeForMoistureMeasurement) {
    
    // is it already time to perform a new moisture check?
    if(IsTimeForMoistureMeasurement) {
        
        /* Store the current time to "remember" when the last moisture measurement took place
         * This information will be needed to decide in later loops of the code if it is time
         * to perform a new measurement
         */
        lastMoistMeasureTime = millis();
        
        // Start the measurement of the current soil moisture
        PerformMoistureMeasurement();
    }
}




// Decide if we need to switch the Dryness Warning LED on or off based on the interpretation of the moisture sensor analog input
void DecisionToSwitchSoilDryWaringLED(int Indicator){


    // remember the moisture indicator in this switch statement if "0" some day no longer means "urgently dry"
    // and "1" does no longer mean "dry"
    // MoistureIndicators[0];
    
    switch(Indicator){ // What kind of soil moisture indicator did we receive?
            
        case 0: // the soil is urgently dry
        case 1: // the soil is dry
            
            // switch on the red dryness indication LED
            digitalWrite(SoilDryWarningLED, HIGH);
            break;
            
        default: // in all the cases where the soil is not "dry" or "urgently dry" no warning LED is needed
            
            // switch of the red dryness indication LED
            digitalWrite(SoilDryWarningLED, LOW);
            break;
    }
}




// Switch on the water pump by switching the transistor
void StartTheWaterPump(){
    
    /* store when the pump action started
     * check how long the self watering action is currently performed
     * check if the soil is already "moist" again
     * stop the watering immediately if the time for the watering is up or the soil is "moist" again to avoid water overflow
     */
    
    unsigned long CurrentMillis = millis(); // recurring check of the current time
    unsigned long PumpBeginningMillis = CurrentMillis; // this value serves to compare start and end time of the watering action
    unsigned long PumpDurationMillis = 10000; // water for 10 seconds. This provides 300 ml of water
    
    while ((CurrentMillis - PumpBeginningMillis < PumpDurationMillis) && (MoistureIndicator != MoistureIndicators[2])) {
        
        // switch on the water pump
        digitalWrite(PumpVoltagePin, HIGH);
        
        // check if the soil is "moist" already;
        PerformMoistureMeasurement();
        
        CurrentMillis = millis();
    }
    
    // stop the water pump
    digitalWrite(PumpVoltagePin, LOW);
}




// Decide if we need to switch on the water pump to perform a self watering action based on the interpretation of the moisture sensor analog input
void DecisionToSwitchWaterPump(int Indicator){
    
    // remember the moisture indicator in this switch statement if "0" some day no longer means "urgently dry"
    // MoistureIndicators[0];
    
    switch (Indicator) {
        case 0: // the soil is "urgently dry"
            
            // start the self watering action
            StartTheWaterPump();
            
            break;
            
        default:
            // do nothing but ensure that there is no power supply to the transistor
            digitalWrite(PumpVoltagePin, LOW);
            
            break;
    }
}


// Transform the current moisture value into a percentage value and send it to a database using http://
void SendMoisturePercentageValueToDatabase(boolean IsTimeToSendData, int MoistAnalogValue){
    
    if (IsTimeToSendData){
        
        // Serial log info
        // debugoutln("SendMoisturePercentageValueToDatabase");
        
        // Transform the current analogInput value for the moisture of the soil into a percentage value
        FullHttpPostTransmission(PercentMoistureValue(MoistAnalogValue));
        
    }
}




// Loop Start #######################################################################################################################




void loop() {
    
    /* Check if it is time to start the measurement of the soil moisture
     * The return of this check is a simple TRUE or FALSE statement
     * We use this statement to pass it on to following functions to decide e.g. if a moisture
     * needs to take place
     */
    boolean MeasureAndDataTransimitionTime = IsTimeForMoistureMeasurement();
    
    /* Start the moisture measurement
     * Cosider the TRUE or FALSE statement from the time check before
     * The return of this moisture measurement is an analog input value
     * This analog input value is then converted into a percentage value in three ranges which lead to an interpretation
     * of the current moisture status of the soil - let's start with green, yellow, red
     */
    MoistureMeasurement(MeasureAndDataTransimitionTime);
    
    /* Decide if the red dryness warning indication LED needs to be swiched on or off based on the moisture
     * interpretation
     */
    DecisionToSwitchSoilDryWaringLED(MoistureIndicator);
    
    /* Decide if the water pump to water the soil automatically should be switched on
     * This decision will be based on the last moisture measurement of the moisture sensor
     * If the soil is "urgently dry" the waterpump will immediately start watering the soil
     */
    DecisionToSwitchWaterPump(MoistureIndicator);
    
    /* Send the moisture data to a central database 
     * from there the moisture value can be displayed in an app or on a website
     * we only store the current percentage value for the moisture in that database
     */
    SendMoisturePercentageValueToDatabase(MeasureAndDataTransimitionTime, MoistureMeasurementResultAnalogInput);
    
    /* After one cycle of the loop has taken place reset the value of the MeasureAndDataTransimitionTime 
     * to avoid unnecessary measures or data transmitions
     */
    MeasureAndDataTransimitionTime = false;
    
}
